// Logisim project SR_with_latch_example.circ as structural Verilog: 3 circuits, main circuit test
module shiftRegister (
  input  SCLR,
  input  SI,
  input  SCK,
  input  RCK,
  output Q8_prime,
  output Q8C,
  output Q1,
  output Q2,
  output Q3,
  output Q4,
  output Q5,
  output Q6,
  output Q7,
  output Q8
);

  wire not_1_out, not_2_out, shift_register_1_p6, shift_register_1_p7, shift_register_1_p8,
       shift_register_1_p9, shift_register_1_p10, shift_register_1_p11, shift_register_1_p12;

  not not_1 (not_1_out, SCLR);
  // Shift_Register shift_register_1: pin names not known; wires that end beside it: not_1_out, 1'b0, 1'b1, SCK, SI, shift_register_1_p6, shift_register_1_p7, shift_register_1_p8, shift_register_1_p9, shift_register_1_p10, shift_register_1_p11, shift_register_1_p12, Q8_prime
  D_Flip_Flop d_ff_1 (.D(shift_register_1_p6), .clk(RCK), .Q(Q1));  // open: Qn, preset, reset
  D_Flip_Flop d_ff_2 (.D(shift_register_1_p8), .clk(RCK), .Q(Q3));  // open: Qn, preset, reset
  D_Flip_Flop d_ff_3 (.D(shift_register_1_p10), .clk(RCK), .Q(Q5));  // open: Qn, preset, reset
  D_Flip_Flop d_ff_4 (.D(shift_register_1_p12), .clk(RCK), .Q(Q7));  // open: Qn, preset, reset
  D_Flip_Flop d_ff_5 (.D(Q8_prime), .clk(not_2_out), .Q(Q8C), .reset(not_1_out));  // open: Qn, preset
  not not_2 (not_2_out, SCK);
  D_Flip_Flop d_ff_6 (.D(shift_register_1_p7), .clk(RCK), .Q(Q2));  // open: Qn, preset, reset
  D_Flip_Flop d_ff_7 (.D(shift_register_1_p9), .clk(RCK), .Q(Q4));  // open: Qn, preset, reset
  D_Flip_Flop d_ff_8 (.D(shift_register_1_p11), .clk(RCK), .Q(Q6));  // open: Qn, preset, reset
  D_Flip_Flop d_ff_9 (.D(Q8_prime), .clk(RCK), .Q(Q8));  // open: Qn, preset, reset
endmodule

module main (
  input  reset,
  input  data0,
  input  in_3,
  input  in_4,
  input  clk,
  input  latch,
  input  in_7
);

  wire clock_1_out, controlled_buffer_1_out, not_1_out, not_2_out, or_1_out, or_2_out, or_3_out, or_4_out,
       or_5_out, or_6_out, shiftregister_1_q8_prime, shiftregister_2_q8_prime, shiftregister_3_q8_prime,
       shiftregister_5_q8_prime, shiftregister_6_q8_prime, shiftregister_7_q8_prime, t_ff_1_qn, t_ff_2_qn,
       t_ff_3_qn, t_ff_4_q, t_ff_5_qn, t_ff_6_qn, t_ff_7_qn, undriven, undriven_2;
  wire [5:0] counter_1_q;
  wire [7:0] shiftregister_1_q1, shiftregister_2_q1, shiftregister_3_q1, shiftregister_4_q1,
       shiftregister_5_q1, shiftregister_6_q1, shiftregister_7_q1, shiftregister_8_q1;

  Clock clock_1 (.out(clock_1_out));
  or or_1 (or_1_out, in_7, clock_1_out);
  assign controlled_buffer_1_out = not_1_out ? or_1_out : 1'bz;  // Controlled_Buffer controlled_buffer_1
  T_Flip_Flop t_ff_1 (.T(1'b1), .clk(controlled_buffer_1_out), .Qn(t_ff_1_qn), .reset(in_4));  // open: Q, preset
  T_Flip_Flop t_ff_2 (.T(1'b1), .clk(t_ff_5_qn), .Qn(t_ff_2_qn), .reset(in_4));  // open: Q, preset
  T_Flip_Flop t_ff_3 (.T(1'b1), .clk(t_ff_6_qn), .Qn(t_ff_3_qn), .reset(in_4));  // open: Q, preset
  T_Flip_Flop t_ff_4 (.T(1'b1), .clk(t_ff_7_qn), .Q(t_ff_4_q), .reset(in_4));  // open: Qn, preset
  LedBar #(.matrixcols(64)) ledbar_1 (
    .led0(shiftregister_1_q1[0]), .led1(shiftregister_1_q1[1]), .led2(shiftregister_1_q1[2]),
    .led3(shiftregister_1_q1[3]), .led4(shiftregister_1_q1[4]), .led5(shiftregister_1_q1[5]),
    .led6(shiftregister_1_q1[6]), .led7(shiftregister_1_q1[7]), .led8(shiftregister_2_q1[0]),
    .led9(shiftregister_2_q1[1]), .led10(shiftregister_2_q1[2]), .led11(shiftregister_2_q1[3]),
    .led12(shiftregister_2_q1[4]), .led13(shiftregister_2_q1[5]), .led14(shiftregister_2_q1[6]),
    .led15(shiftregister_2_q1[7]), .led16(shiftregister_3_q1[0]), .led17(shiftregister_3_q1[1]),
    .led18(shiftregister_3_q1[2]), .led19(shiftregister_3_q1[3]), .led20(shiftregister_3_q1[4]),
    .led21(shiftregister_3_q1[5]), .led22(shiftregister_3_q1[6]), .led23(shiftregister_3_q1[7]),
    .led24(shiftregister_4_q1[0]), .led25(shiftregister_4_q1[1]), .led26(shiftregister_4_q1[2]),
    .led27(shiftregister_4_q1[3]), .led28(shiftregister_4_q1[4]), .led29(shiftregister_4_q1[5]),
    .led30(shiftregister_4_q1[6]), .led31(shiftregister_4_q1[7]), .led32(shiftregister_5_q1[0]),
    .led33(shiftregister_5_q1[1]), .led34(shiftregister_5_q1[2]), .led35(shiftregister_5_q1[3]),
    .led36(shiftregister_5_q1[4]), .led37(shiftregister_5_q1[5]), .led38(shiftregister_5_q1[6]),
    .led39(shiftregister_5_q1[7]), .led40(shiftregister_6_q1[0]), .led41(shiftregister_6_q1[1]),
    .led42(shiftregister_6_q1[2]), .led43(shiftregister_6_q1[3]), .led44(shiftregister_6_q1[4]),
    .led45(shiftregister_6_q1[5]), .led46(shiftregister_6_q1[6]), .led47(shiftregister_6_q1[7]),
    .led48(shiftregister_7_q1[0]), .led49(shiftregister_7_q1[1]), .led50(shiftregister_7_q1[2]),
    .led51(shiftregister_7_q1[3]), .led52(shiftregister_7_q1[4]), .led53(shiftregister_7_q1[5]),
    .led54(shiftregister_7_q1[6]), .led55(shiftregister_7_q1[7]), .led56(shiftregister_8_q1[0]),
    .led57(shiftregister_8_q1[1]), .led58(shiftregister_8_q1[2]), .led59(shiftregister_8_q1[3]),
    .led60(shiftregister_8_q1[4]), .led61(shiftregister_8_q1[5]), .led62(shiftregister_8_q1[6]),
    .led63(shiftregister_8_q1[7]));
  Counter #(.max('h3f), .trigger("falling"), .width(6)) counter_1 (
    .clr(in_4), .load(1'b0), .up(1'b1), .count(1'b1), .clk(controlled_buffer_1_out), .Q(counter_1_q));  // open: D, carry
  T_Flip_Flop t_ff_5 (.T(1'b1), .clk(t_ff_1_qn), .Qn(t_ff_5_qn), .reset(in_4));  // open: Q, preset
  T_Flip_Flop t_ff_6 (.T(1'b1), .clk(t_ff_2_qn), .Qn(t_ff_6_qn), .reset(in_4));  // open: Q, preset
  T_Flip_Flop t_ff_7 (.T(1'b1), .clk(t_ff_3_qn), .Qn(t_ff_7_qn), .reset(in_4));  // open: Q, preset
  not not_1 (not_1_out, t_ff_4_q);
  ROM #(.addrWidth(6), .dataWidth(1)) rom_1 (.addr(counter_1_q));  // open: data
  not not_2 (not_2_out, in_4);
  Pull_Resistor pull_resistor_1 (.node(controlled_buffer_1_out));
  or or_2 (or_2_out, in_3, t_ff_4_q);
  or or_3 (or_3_out, reset, not_2_out);
  or or_4 (or_4_out, data0, undriven);
  or or_5 (or_5_out, clk, controlled_buffer_1_out);
  or or_6 (or_6_out, latch, or_2_out);
  shiftRegister shiftregister_1 (
    .SCLR(or_3_out), .SI(or_4_out), .SCK(or_5_out), .RCK(or_6_out), .Q8_prime(shiftregister_1_q8_prime),
    .Q1(shiftregister_1_q1[0]), .Q2(shiftregister_1_q1[1]), .Q3(shiftregister_1_q1[2]),
    .Q4(shiftregister_1_q1[3]), .Q5(shiftregister_1_q1[4]), .Q6(shiftregister_1_q1[5]),
    .Q7(shiftregister_1_q1[6]), .Q8(shiftregister_1_q1[7]));  // open: Q8C
  shiftRegister shiftregister_2 (
    .SCLR(or_3_out), .SI(shiftregister_1_q8_prime), .SCK(or_5_out), .RCK(or_6_out),
    .Q8_prime(shiftregister_2_q8_prime), .Q1(shiftregister_2_q1[0]), .Q2(shiftregister_2_q1[1]),
    .Q3(shiftregister_2_q1[2]), .Q4(shiftregister_2_q1[3]), .Q5(shiftregister_2_q1[4]),
    .Q6(shiftregister_2_q1[5]), .Q7(shiftregister_2_q1[6]), .Q8(shiftregister_2_q1[7]));  // open: Q8C
  shiftRegister shiftregister_3 (
    .SCLR(or_3_out), .SI(shiftregister_2_q8_prime), .SCK(or_5_out), .RCK(or_6_out),
    .Q8_prime(shiftregister_3_q8_prime), .Q1(shiftregister_3_q1[0]), .Q2(shiftregister_3_q1[1]),
    .Q3(shiftregister_3_q1[2]), .Q4(shiftregister_3_q1[3]), .Q5(shiftregister_3_q1[4]),
    .Q6(shiftregister_3_q1[5]), .Q7(shiftregister_3_q1[6]), .Q8(shiftregister_3_q1[7]));  // open: Q8C
  shiftRegister shiftregister_4 (
    .SCLR(or_3_out), .SI(shiftregister_3_q8_prime), .SCK(or_5_out), .RCK(or_6_out),
    .Q1(shiftregister_4_q1[0]), .Q2(shiftregister_4_q1[1]), .Q3(shiftregister_4_q1[2]),
    .Q4(shiftregister_4_q1[3]), .Q5(shiftregister_4_q1[4]), .Q6(shiftregister_4_q1[5]),
    .Q7(shiftregister_4_q1[6]), .Q8(shiftregister_4_q1[7]));  // open: Q8_prime, Q8C
  shiftRegister shiftregister_5 (
    .SCLR(or_3_out), .SI(undriven_2), .SCK(or_5_out), .RCK(or_6_out), .Q8_prime(shiftregister_5_q8_prime),
    .Q1(shiftregister_5_q1[0]), .Q2(shiftregister_5_q1[1]), .Q3(shiftregister_5_q1[2]),
    .Q4(shiftregister_5_q1[3]), .Q5(shiftregister_5_q1[4]), .Q6(shiftregister_5_q1[5]),
    .Q7(shiftregister_5_q1[6]), .Q8(shiftregister_5_q1[7]));  // open: Q8C
  shiftRegister shiftregister_6 (
    .SCLR(or_3_out), .SI(shiftregister_5_q8_prime), .SCK(or_5_out), .RCK(or_6_out),
    .Q8_prime(shiftregister_6_q8_prime), .Q1(shiftregister_6_q1[0]), .Q2(shiftregister_6_q1[1]),
    .Q3(shiftregister_6_q1[2]), .Q4(shiftregister_6_q1[3]), .Q5(shiftregister_6_q1[4]),
    .Q6(shiftregister_6_q1[5]), .Q7(shiftregister_6_q1[6]), .Q8(shiftregister_6_q1[7]));  // open: Q8C
  shiftRegister shiftregister_7 (
    .SCLR(or_3_out), .SI(shiftregister_6_q8_prime), .SCK(or_5_out), .RCK(or_6_out),
    .Q8_prime(shiftregister_7_q8_prime), .Q1(shiftregister_7_q1[0]), .Q2(shiftregister_7_q1[1]),
    .Q3(shiftregister_7_q1[2]), .Q4(shiftregister_7_q1[3]), .Q5(shiftregister_7_q1[4]),
    .Q6(shiftregister_7_q1[5]), .Q7(shiftregister_7_q1[6]), .Q8(shiftregister_7_q1[7]));  // open: Q8C
  shiftRegister shiftregister_8 (
    .SCLR(or_3_out), .SI(shiftregister_7_q8_prime), .SCK(or_5_out), .RCK(or_6_out),
    .Q1(shiftregister_8_q1[0]), .Q2(shiftregister_8_q1[1]), .Q3(shiftregister_8_q1[2]),
    .Q4(shiftregister_8_q1[3]), .Q5(shiftregister_8_q1[4]), .Q6(shiftregister_8_q1[5]),
    .Q7(shiftregister_8_q1[6]), .Q8(shiftregister_8_q1[7]));  // open: Q8_prime, Q8C

  // Notes on the sheet:
  //   contents of rom_1 (hex, n*v repeats v):
  //   1 15*0 1 1 0 0 1 1 0 0 4*1 4*0 1 0 1 0 1 0 1 9*0 1 1 0 0 1 0 1 0 0 0 1 1 0 1 0 1
endmodule

module test (
  input  in_1,
  input  in_2,
  input  in_3
);

  wire clock_1_out, not_1_out, shift_register_1_p6, shift_register_1_p7, shift_register_1_p8,
       shift_register_1_p9, shift_register_1_p10, shift_register_1_p11, shift_register_1_p12,
       shift_register_1_p13, shiftregister_1_q1, shiftregister_1_q2, shiftregister_1_q3, shiftregister_1_q4,
       shiftregister_1_q5, shiftregister_1_q6, shiftregister_1_q7, shiftregister_1_q8;

  Clock clock_1 (.out(clock_1_out));
  not not_1 (not_1_out, in_1);
  // Shift_Register shift_register_1: pin names not known; wires that end beside it: not_1_out, 1'b0, 1'b1, clock_1_out, in_2, shift_register_1_p6, shift_register_1_p7, shift_register_1_p8, shift_register_1_p9, shift_register_1_p10, shift_register_1_p11, shift_register_1_p12, shift_register_1_p13
  shiftRegister shiftregister_1 (
    .SCLR(in_1), .SI(in_2), .SCK(clock_1_out), .RCK(in_3), .Q1(shiftregister_1_q1), .Q2(shiftregister_1_q2),
    .Q3(shiftregister_1_q3), .Q4(shiftregister_1_q4), .Q5(shiftregister_1_q5), .Q6(shiftregister_1_q6),
    .Q7(shiftregister_1_q7), .Q8(shiftregister_1_q8));  // open: Q8_prime, Q8C
  LED led_1 (.in(shift_register_1_p6));
  LED led_2 (.in(shift_register_1_p7));
  LED led_3 (.in(shift_register_1_p8));
  LED led_4 (.in(shift_register_1_p9));
  LED led_5 (.in(shift_register_1_p10));
  LED led_6 (.in(shift_register_1_p11));
  LED led_7 (.in(shift_register_1_p12));
  LED led_8 (.in(shift_register_1_p13));
  LED led_9 (.in(shiftregister_1_q1));
  LED led_10 (.in(shiftregister_1_q2));
  LED led_11 (.in(shiftregister_1_q3));
  LED led_12 (.in(shiftregister_1_q4));
  LED led_13 (.in(shiftregister_1_q5));
  LED led_14 (.in(shiftregister_1_q6));
  LED led_15 (.in(shiftregister_1_q7));
  LED led_16 (.in(shiftregister_1_q8));
endmodule
